# Fritzing sketch IO Expander (saved by Fritzing 0.9.6b)
breadboards: 1

parts:
  IC1 = IC, DIP package, 18 pins [chip_label=IC]
  LED1 = RGB LED (com. cathode, rbg) [package="5 mm [THT]"]
  LED2 = RGB LED (com. cathode, rbg) [package="5 mm [THT]"]
  R1 = Resistor [tolerance=±5% power=0.25 resistance=160 package=THT]
  R2 = Resistor [tolerance=±5% power=0.25 resistance=160 package=THT]
  R3 = Resistor [tolerance=±5% power=0.25 resistance=160 package=THT]
  R4 = Resistor [tolerance=±5% power=0.25 resistance=160 package=THT]
  R5 = Resistor [tolerance=±5% power=0.25 resistance=160 package=THT]
  R6 = Resistor [tolerance=±5% power=0.25 resistance=160 package=THT]
  S1 = SWITCH-MOMENTARY-2 [package=tactile-pth]
  S2 = SWITCH-MOMENTARY-2 [package=tactile-pth]
  R7 = Resistor [tolerance=±5% power=0.25 resistance=2000 package=THT]
  R8 = Resistor [tolerance=±5% power=0.25 resistance=2000 package=THT]
  J1 = female pin header, 4 pins [form="♀ (female)"]

nets:
  N1: IC1.pin1, R7.Pin_1, J1.pin2
  N2: IC1.pin2, R8.Pin_1, J1.pin3
  GND: IC1.pin3, IC1.pin4, IC1.pin5, IC1.pin9, LED1.common_cathode, LED2.common_cathode, S1.2, S2.2, J1.pin4
  3.3V: IC1.pin6, IC1.pin18, R7.Pin_0, R8.Pin_0, J1.pin1
  N3: IC1.pin10, R1.Pin_1
  N4: IC1.pin11, R2.Pin_1
  N5: IC1.pin12, R3.Pin_1
  N6: IC1.pin13, R5.Pin_1
  N7: IC1.pin14, R6.Pin_1
  N8: IC1.pin15, R4.Pin_1
  N9: IC1.pin16, S2.1
  N10: IC1.pin17, S1.1
  N11: LED1.red_anode, R1.Pin_0
  N12: LED1.blue_anode, R2.Pin_0
  N13: LED1.green_anode, R3.Pin_0
  N14: LED2.red_anode, R5.Pin_0
  N15: LED2.blue_anode, R6.Pin_0
  N16: LED2.green_anode, R4.Pin_0
